# Fritzing sketch electret (saved by Fritzing 1.0.8)
breadboards: 1

parts:
  SOM1 = Daisy Seed [chip_label=IC package="DIP (Dual Inline) [THT]"]
  Part2 = Adafruit MAX9814 Electret Microphone Amplifier [part_number="Adafruit #1713"]

nets:
  N1: SOM1.pin_16, Part2.OUTPUT
  N2: SOM1.pin_20, SOM1.pin_40, Part2.GND
  N3: SOM1.pin_38, Part2.VDD

custom parts:
  Daisy Seed: Daisy is an embedded platform for music. It features everything you need for creating high fidelity audio hardware devices. Just plug in a USB cable and start making sound! No soldering required.
  Adafruit MAX9814 Electret Microphone Amplifier: Add an ear to your project with this well-designed electret microphone amplifier with AGC. This fully assembled and tested board comes with a 20-20KHz electret microphone soldered on. For the amplification, we use the Maxim MAX9814, a specialty chip that is designed for amplifying electret microphones in situations where the loudness of the audio isn't predictable. This fancy microphone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
